# Fritzing sketch solar (saved by Fritzing 0.8.7b)
perfboards: 1

parts:
  VCC1 = 4 x AAA Battery Mount  # not connected
  U1 = atmega328 [package=dip]
  U3 = RF-LINK_TX [package=rf-link_tx]
  D1 = SOLAR-IXYS [package=solarbit-12x1]
  D3 = SOLAR-IXYS [package=solarbit-12x1]
  R3 = Resistor [tolerance=±5% resistance=10k package=THT]  # not connected
  ANT1 = Antenna
  C5 = Electrolytic Capacitor [capacitance=10µF voltage=16V package="100 mil [THT, electrolytic]"]
  D4 = Rectifier Diode [part_number=1N4001 package="300 mil [THT]"]  # not connected
  C6 = Ceramic Capacitor [capacitance=100nF package="100 mil [THT, multilayer]"]
  J5 = male pin header, 3 pins [form="♂ (male)"]
  R5 = Resistor [tolerance=±5% resistance=100k package=THT]  # not connected
  J7 = Screw terminal - 2 pins [package=THT]  # not connected
  J2 = male pin header, 4 pins [form="♂ (male)"]
  J6 = male pin header, 2 pins [form="♂ (male)"]
  J8 = Screw terminal - 2 pins [package=THT]  # not connected
  J9 = Screw terminal - 2 pins [package=THT]  # not connected
  R6 = Resistor [tolerance=±5% resistance=10k package=THT]
  J3 = male pin header, 3 pins [form="♂ (male)"]  # not connected
  R7 = Resistor [tolerance=±5% resistance=10k package=THT]
  T1 = LM35 Temperature Sensor [package="TO92 [THT]"]  # not connected
  C7 = Ceramic Capacitor [capacitance=100nF package="100 mil [THT, multilayer]"]
  C8 = Ceramic Capacitor [capacitance=100nF package="100 mil [THT, multilayer]"]  # not connected
  C9 = Ceramic Capacitor [capacitance=100nF package="100 mil [THT, multilayer]"]  # not connected
  R10 = Resistor [tolerance=±5% resistance=10k package=THT]

nets:
  N1: U1.VCC, U1.AVCC, C5.+, C7.0
  N2: U1.GND#7, U3.GND, C5.-, J5.pin3, C7.1
  N3: U1.D7, U3.DATA, J5.pin1
  N4: U1.D8, U3.+5V, J5.pin2
  N5: U1.GND#21, R10.Pin_0
  N6: U3.ANT, ANT1.antenna_lead
  N7: D1.A, D3.C
  N8: D1.C, J6.pin1
  N9: D3.A, J6.pin2
  N10: C6.0, J2.pin1
  N11: C6.1, J2.pin2
  N12: R6.Pin_1, R7.Pin_0
