# Fritzing sketch arduino (saved by Fritzing 0.9.0b)
stripboards: 1

parts:
  U1 = atmega328 [package=dip]
  ANT1 = Antenna
  C5 = Electrolytic Capacitor [capacitance=10µF voltage=16V package="100 mil [THT, electrolytic]"]
  C6 = Ceramic Capacitor [capacitance=100nF package="100 mil [THT, multilayer]"]
  J6 = male pin header, 1 pin [form="♂ (male)"]
  J9 = male pin header, 1 pin [form="♂ (male)"]
  R6 = Resistor [tolerance=±5% resistance=100k package=THT]
  U4 = mystery part, 8 pins [chip_label=MCP4131]
  J2 = male pin header, 3 pins [form="♂ (male)"]
  J10 = male pin header, 3 pins [form="♂ (male)"]
  C10 = Ceramic Capacitor [capacitance=100nF package="100 mil [THT, multilayer]"]
  U5 = RF-LINK_RX [package=rf-link_rx]
  J11 = Screw terminal - 2 pins [package=THT]
  BLUEFRUIT1 = Adafruit Bluefruit EZ-LINK v1.0
  J12 = Screw terminal - 2 pins [package=THT]
  J13 = Screw terminal - 2 pins [package=THT]
  J14 = Screw terminal - 2 pins [package=THT]
  J15 = Screw terminal - 2 pins [package=THT]
  METER1 = 7-Segment Panel Voltmeter

nets:
  N1: U1.RESET, R6.Pin_1, J10.pin1
  N2: U1.D0_(RX), J10.pin2
  N3: U1.D1_(TX), J10.pin3, BLUEFRUIT1.RX, J13.pin2
  N4: U1.VCC, U1.AVCC, C5.+, C6.0, J9.pin1, U4.pin5, U4.pin8, C10.1, BLUEFRUIT1.3v, J12.pin1
  GND: U1.GND, C5.-, C6.1, J6.pin1, R6.Pin_0, U4.pin4, U4.pin7, C10.0, U5.GND, J11.pin1, BLUEFRUIT1.GND, J13.pin1, J15.pin2, METER1.V-
  N5: U1.D10_(PWM), U4.pin1
  N6: U1.D11_(PWM), U4.pin3, J2.pin3
  N7: U1.D12, J2.pin2
  N8: U1.D13, U4.pin2, J2.pin1
  N9: U1.A1, U5.DATA, J14.pin2
  N10: U1.A3, U5.+5V, J14.pin1
  N11: ANT1.antenna_lead, U5.ANT
  N12: U4.pin6, J11.pin2, METER1.V+

custom parts:
  Adafruit Bluefruit EZ-LINK v1.0: Bluefruit EZ-LINK, Bluetooth Serial Link & Arduino Programmer
  7-Segment Panel Voltmeter: 7-Segment Panel Voltmeter (4.5 - 30V)
