# Fritzing sketch power (saved by Fritzing 0.9.0b)
stripboards: 1

parts:
  J1 = Screw terminal - 2 pins [package=THT]
  J2 = Screw terminal - 2 pins [package=THT]  # not connected
  J3 = Screw terminal - 2 pins [package=THT]
  D1 = Rectifier Diode [part_number=1N4001 package="300 mil [THT]"]  # not connected
  C1 = Electrolytic Capacitor [capacitance=1µF package="100 mil [THT, electrolytic]"]
  2n7000_N_mosfet = mystery part, 3 pins [chip_label=?]
  3_3v_Regulator = mystery part, 3 pins [chip_label=?]
  R1_1M_dark_->_8k_light = Photocell (LDR) [package=THT]
  VCC1 = 4 x AAA Battery Mount
  D2 = SOLAR-IXYS [package=solarbit-12x1]  # not connected
  Bypass_mosfet_switch = Screw terminal - 2 pins [package=THT]
  R1 = Resistor [tolerance=±5% resistance=10k package=THT]

nets:
  N1: J1.pin1, C1.+, 3_3v_Regulator.pin1
  N2: J1.pin2, C1.-, 2n7000_N_mosfet.pin1, 3_3v_Regulator.pin2, Bypass_mosfet_switch.pin1
  N3: J3.pin1, 2n7000_N_mosfet.pin3, VCC1.-, Bypass_mosfet_switch.pin2, R1.Pin_1
  N4: 2n7000_N_mosfet.pin2, R1_1M_dark_->_8k_light.pin_0, R1.Pin_0
  N5: 3_3v_Regulator.pin3, R1_1M_dark_->_8k_light.pin_1, VCC1.+

notes:
  mA
  V
  Solar negative connected to battery negative
  - Negatives after diode go through mosfet.
